# Fritzing sketch HardwareLayout (saved by Fritzing 0.9.3b)

parts:
  J1 = Basic Servo
  J2 = Basic Servo
  J3 = Basic Servo
  Part1 = Arduino Due (Rev2b)

nets:
  N1: J1.pulse, Part1.D8_PWM
  N2: J2.pulse, Part1.D9_PWM
  N3: J3.pulse, Part1.D10_PWM/SS0

notes:
  5V - 0.7A Power Supply
